// Logisim project projet_etu.circ as structural Verilog: 9 circuits, main circuit main
module main (
  input  Reset,
  input  ResetRAM
);

  wire Clock, Clock_out, CTRL, Exec, Fetch, getcst_1_imm, Load, ramctrl_1_memload, ramctrl_1_memstore, Store,
       WriteReg;
  wire [2:0] GetOp;
  wire [15:0] Addr, alu_1_output, Arg1, getcst_1_cst, JMP_Address, MemIN, multiplexer_1_out, PC, R0, R1, R2,
       R3, R4, R5, R6, R7, registres_1_out_sr2;
  wire [31:0] bit_extender_1_out, IR, MemOUT;

  Clock u_Clock (.out(Clock_out));
  Seq seq_1 (.ClockOrig(Clock_out), .reset(Reset), .Fetch(Fetch), .Exec(Exec), .Clock(Clock));
  LED led_1 (.in(Clock_out));
  RegPC regpc_1 (.JMP_Address(JMP_Address), .Cond(1'b0), .CTRL(CTRL), .Clock(Exec), .Reset(Reset), .PC(PC));
  // Probe on PC
  GetAddr getaddr_1 (.PC(PC), .Addr(Addr), .Fetch(Fetch), .Load(Load), .Store(Store), .Arg1(Arg1));
  // Probe on Addr
  LED led_2 (.in(Fetch));
  LED led_3 (.in(Exec));
  // Probe on MemIN
  assign bit_extender_1_out = {{16{MemIN[15]}}, MemIN};  // Bit_Extender bit_extender_1
  // Probe on PC
  // Probe on IR
  DecodeIR decodeir_1 (
    .CTRL(CTRL), .WriteReg(WriteReg), .IR(IR), .GetOp(GetOp), .JMPAddress(JMP_Address), .Store(Store),
    .Load(Load));
  RamCtrl ramctrl_1 (
    .Store(Store), .Fetch(Fetch), .Exec(Exec), .Load(Load), .MemStore(ramctrl_1_memstore),
    .MemLoad(ramctrl_1_memload), .Clock(Clock));
  // Probe on MemOUT
  RAM #(.addrWidth(16), .dataWidth(32), .bus("separate")) ram_1 (
    .addr(Addr), .din(bit_extender_1_out), .data(MemOUT), .str(ramctrl_1_memstore), .clk(ramctrl_1_memstore),
    .ld(ramctrl_1_memload), .clr(ResetRAM));  // open: sel
  // Probe on R0
  // Probe on R3
  // Probe on R6
  Register #(.width(32), .trigger("falling")) RegIR (.D(MemOUT), .Q(IR), .clk(Fetch), .clr(Reset));  // open: en
  // Probe on R1
  // Probe on R4
  // Probe on R7
  // Probe on IR
  // Probe on R2
  // Probe on R5
  // Probe on IR[8:6]
  // Probe on IR[11:9]
  // Probe on IR[14:12]
  // Probe on getcst_1_cst
  GetCst getcst_1 (.IR(IR), .Cst(getcst_1_cst), .Imm(getcst_1_imm));
  Multiplexer #(.width(16), .enable("false")) multiplexer_1 (
    .in0(alu_1_output), .in1(MemOUT[15:0]), .out(multiplexer_1_out), .sel(Load));
  Registres registres_1 (
    .SR1(IR[11:9]), .IN(multiplexer_1_out), .SR2(IR[14:12]), .WriteReg(WriteReg), .OUT_SR1(Arg1),
    .OUT_SR2(registres_1_out_sr2), .OUT_DR(MemIN), .R0(R0), .R1(R1), .R2(R2), .R3(R3), .R4(R4), .R5(R5),
    .R6(R6), .R7(R7), .Reset(Reset), .Clock(Exec), .DR(IR[8:6]));
  // Probe on Arg1
  // Probe on registres_1_out_sr2
  ALU alu_1 (
    .Input1(Arg1), .Input2(registres_1_out_sr2), .Cst(getcst_1_cst), .Imm(getcst_1_imm), .op(GetOp),
    .Output(alu_1_output));
  // Probe on multiplexer_1_out
  // Probe on R0
  // Probe on R1
  // Probe on R2
  // Probe on R3
  // Probe on R4
  // Probe on R5
  // Probe on R6
  // Probe on R7
  // Probe on alu_1_output

  // Notes on the sheet:
  //   RAM
endmodule

module ALU (
  input  [15:0] Input1,
  input  [15:0] Input2,
  input  [15:0] Cst,
  input  Imm,
  input  [2:0] op,
  output [15:0] Output
);

  wire [15:0] adder_1_out, and_1_out, multiplexer_2_out, multiplier_1_cout, or_1_out, shifter_1_out,
       shifter_2_out, subtractor_1_out, xor_1_out;

  Adder #(.width(16)) adder_1 (.a(Input1), .b(multiplexer_2_out), .out(adder_1_out));  // open: cin, cout
  Subtractor #(.width(16)) subtractor_1 (.a(Input1), .b(multiplexer_2_out), .out(subtractor_1_out));  // open: bin, bout
  Multiplier #(.width(16)) multiplier_1 (
    .a(Input1), .b(multiplexer_2_out), .cout(multiplier_1_cout));  // open: out, cin
  assign and_1_out = Input1 & multiplexer_2_out;  // AND_Gate and_1, 16 bits wide
  assign or_1_out = Input1 | multiplexer_2_out;  // OR_Gate or_1, 16 bits wide
  Multiplexer #(.select(3), .width(16), .enable("false")) multiplexer_1 (
    .in0(adder_1_out), .in1(subtractor_1_out), .in2(multiplier_1_cout), .in3(and_1_out), .in4(or_1_out),
    .in5(xor_1_out), .in6(shifter_1_out), .in7(shifter_2_out), .out(Output), .sel(op));
  Multiplexer #(.width(16), .enable("false")) multiplexer_2 (
    .in0(Input2), .in1(Cst), .out(multiplexer_2_out), .sel(Imm));
  assign xor_1_out = Input1 ^ multiplexer_2_out;  // XOR_Gate xor_1, 16 bits wide
  Shifter #(.width(16)) shifter_1 (.in(Input1), .\dist (multiplexer_2_out[3:0]), .out(shifter_1_out));
  Shifter #(.width(16), .shift("lr")) shifter_2 (.in(Input1), .\dist (multiplexer_2_out[3:0]), .out(shifter_2_out));

  // Notes on the sheet:
  //   MUL pour asm
  //   Décalage à gauche/droite sur 4 bits
endmodule

module DecodeIR (
  input  [31:0] IR,
  output WriteReg,
  output Store,
  output Load,
  output CTRL,
  output [2:0] GetOp,
  output [15:0] JMPAddress
);

  wire decoder_1_out0, decoder_1_out1, not_1_out;

  Decoder #(.select(2)) decoder_1 (
    .out0(decoder_1_out0), .out1(decoder_1_out1), .out3(CTRL), .sel(IR[1:0]));  // open: out2, en
  not not_1 (not_1_out, IR[2]);
  and and_1 (Store, decoder_1_out1, IR[2]);
  and and_2 (Load, decoder_1_out1, not_1_out);
  or or_1 (WriteReg, decoder_1_out0, Load);

  assign GetOp = IR[4:2];
  assign JMPAddress = IR[31:16];
endmodule

module GetAddr (
  input  [15:0] Arg1,
  input  [15:0] PC,
  input  Load,
  input  Store,
  input  Fetch,
  output [15:0] Addr
);

  Multiplexer #(.width(16), .enable("false")) multiplexer_1 (.in0(Arg1), .in1(PC), .out(Addr), .sel(Fetch));
endmodule

module GetCst (
  input  [31:0] IR,
  output [15:0] Cst,
  output Imm
);


  assign Cst = IR[31:16];
  assign Imm = IR[5];
endmodule

module RamCtrl (
  input  Clock,
  input  Exec,
  input  Fetch,
  input  Load,
  input  Store,
  output MemLoad,
  output MemStore
);

  wire and_1_out;

  and and_1 (and_1_out, Exec, Load);
  and and_2 (MemStore, Exec, Clock, Store);
  or or_1 (MemLoad, Fetch, and_1_out);
endmodule

module Registres (
  input  [15:0] IN,
  input  [2:0] SR1,
  input  WriteReg,
  input  [2:0] SR2,
  input  Clock,
  input  Reset,
  input  [2:0] DR,
  output [15:0] R0,
  output [15:0] OUT_SR1,
  output [15:0] R1,
  output [15:0] R2,
  output [15:0] R3,
  output [15:0] OUT_SR2,
  output [15:0] R4,
  output [15:0] R5,
  output [15:0] OUT_DR,
  output [15:0] R6,
  output [15:0] R7
);

  wire decoder_1_out0, decoder_1_out1, decoder_1_out2, decoder_1_out3, decoder_1_out4, decoder_1_out5,
       decoder_1_out6, decoder_1_out7;

  Decoder #(.select(3), .disabled(0)) decoder_1 (
    .out0(decoder_1_out0), .out1(decoder_1_out1), .out2(decoder_1_out2), .out3(decoder_1_out3),
    .out4(decoder_1_out4), .out5(decoder_1_out5), .out6(decoder_1_out6), .out7(decoder_1_out7), .sel(DR),
    .en(WriteReg));
  Register #(.width(16), .trigger("falling")) u_R0 (.D(IN), .en(decoder_1_out0), .Q(R0), .clk(Clock), .clr(Reset));
  Register #(.width(16), .trigger("falling")) u_R1 (.D(IN), .en(decoder_1_out1), .Q(R1), .clk(Clock), .clr(Reset));
  Register #(.width(16), .trigger("falling")) u_R2 (.D(IN), .en(decoder_1_out2), .Q(R2), .clk(Clock), .clr(Reset));
  Register #(.width(16), .trigger("falling")) u_R3 (.D(IN), .en(decoder_1_out3), .Q(R3), .clk(Clock), .clr(Reset));
  Register #(.width(16), .trigger("falling")) u_R4 (.D(IN), .en(decoder_1_out4), .Q(R4), .clk(Clock), .clr(Reset));
  Register #(.width(16), .trigger("falling")) u_R5 (.D(IN), .en(decoder_1_out5), .Q(R5), .clk(Clock), .clr(Reset));
  Register #(.width(16), .trigger("falling")) u_R6 (.D(IN), .en(decoder_1_out6), .Q(R6), .clk(Clock), .clr(Reset));
  Register #(.width(16), .trigger("falling")) u_R7 (.D(IN), .en(decoder_1_out7), .Q(R7), .clk(Clock), .clr(Reset));
  Multiplexer #(.select(3), .width(16), .enable("false")) multiplexer_1 (
    .in0(R0), .in1(R1), .in2(R2), .in3(R3), .in4(R4), .in5(R5), .in6(R6), .in7(R7), .out(OUT_SR1), .sel(SR1));
  Multiplexer #(.select(3), .width(16), .enable("false")) multiplexer_2 (
    .in0(R0), .in1(R1), .in2(R2), .in3(R3), .in4(R4), .in5(R5), .in6(R6), .in7(R7), .out(OUT_SR2), .sel(SR2));
  Multiplexer #(.select(3), .width(16), .enable("false")) multiplexer_3 (
    .in0(R0), .in1(R1), .in2(R2), .in3(R3), .in4(R4), .in5(R5), .in6(R6), .in7(R7), .out(OUT_DR), .sel(DR));
endmodule

module RegPC (
  input  [15:0] JMP_Address,
  input  Cond,
  input  CTRL,
  input  Clock,
  input  Reset,
  output [15:0] PC
);

  wire [15:0] adder_1_out;

  Adder #(.width(16)) adder_1 (.a(PC), .b(16'h1), .out(adder_1_out));  // open: cin, cout
  Register #(.width(16), .trigger("falling")) u_PC (.D(adder_1_out), .Q(PC), .clk(Clock), .clr(Reset));  // open: en
endmodule

module Seq (
  input  ClockOrig,
  input  reset,
  output Fetch,
  output Exec,
  output Clock
);

  Register #(.width(1), .trigger("falling")) register_1 (
    .D(Fetch), .Q(Exec), .clk(ClockOrig), .clr(reset));  // open: en
  not not_1 (Fetch, Exec);
  buf buffer_1 (Clock, ClockOrig);
endmodule
